// Digital circuit 8-Bit GPR.dig as structural Verilog
module _8_Bit_GPR (
  input  clk,
  input  [1:0] ctrl,
  input  [1:0] Register_Sel,
  input  [7:0] Input,
  output [7:0] \output 
);

  wire and_1_out, and_2_out, and_3_out, and_4_out, decoder_1_out_0, decoder_1_out_1, decoder_1_out_2,
       decoder_1_out_3;
  wire [7:0] R_0_p4, R_1_p4, R_2_p4, R_3_p4;

  Decoder #(.Selector_Bits(2)) decoder_1 (
    .sel(Register_Sel), .out_0(decoder_1_out_0), .out_1(decoder_1_out_1), .out_2(decoder_1_out_2),
    .out_3(decoder_1_out_3));
  and and_1 (and_1_out, decoder_1_out_0, clk);
  and and_2 (and_2_out, decoder_1_out_1, clk);
  and and_3 (and_3_out, decoder_1_out_2, clk);
  and and_4 (and_4_out, decoder_1_out_3, clk);
  // _8_Bit R_0: pin names not known; wires that end beside it: and_1_out, ctrl, Input, R_0_p4
  // _8_Bit R_1: pin names not known; wires that end beside it: and_2_out, ctrl, Input, R_1_p4
  // _8_Bit R_2: pin names not known; wires that end beside it: and_3_out, ctrl, Input, R_2_p4
  // _8_Bit R_3: pin names not known; wires that end beside it: and_4_out, ctrl, Input, R_3_p4
  Multiplexer #(.Selector_Bits(2), .Bits(8)) multiplexer_1 (
    .sel(Register_Sel), .in_0(R_0_p4), .in_1(R_1_p4), .in_2(R_2_p4), .in_3(R_3_p4), .out(\output ));

  // Notes on the sheet:
  //   ctrl: 00->Load
  //   01->Store
  //   10->Clear
  //   11->Set FF
  //   00->Load
  //   01->Store
  //   10->Clear
  //   11->Set FF
  //   GPR
endmodule
