// Digital circuit SRAM.dig as structural Verilog
module SRAM (
  input  [3:0] ADDR,
  input  [7:0] DATAIN,
  input  clk,
  input  STR,
  input  LD,
  output [7:0] Output
);

  RAMDualPort #(.AddrBits(4), .Bits(8)) ramdualport_1 (.A(ADDR), .Din(DATAIN), .str(STR), .C(clk), .ld(LD), .D(Output));
endmodule
